// Logisim project 4stage_pipeline.circ as structural Verilog: 1 circuit, main circuit main
module main (
  input  Clear_memory,
  input  [31:0] in_2,
  input  RF_Demux,
  input  RF_Mux2,
  input  RF_Mux1,
  input  ALU_Mux,
  input  MUXB,
  input  MUXY,
  output Addition_cary,
  output out_10
);

  wire clock_1_out, comparator_2_eq, comparator_3_eq, demultiplexer_1_out0, demultiplexer_1_out1,
       demultiplexer_1_out2, demultiplexer_1_out3, demultiplexer_1_out4, demultiplexer_1_out5,
       demultiplexer_1_out6, demultiplexer_1_out7, demultiplexer_1_out8, demultiplexer_1_out9,
       demultiplexer_1_out10, demultiplexer_1_out11, demultiplexer_1_out12, demultiplexer_1_out13,
       demultiplexer_1_out14, demultiplexer_1_out15, demultiplexer_1_out16, demultiplexer_1_out17,
       demultiplexer_1_out18, demultiplexer_1_out19, demultiplexer_1_out20, demultiplexer_1_out21,
       demultiplexer_1_out22, demultiplexer_1_out23, demultiplexer_1_out24, demultiplexer_1_out25,
       demultiplexer_1_out26, demultiplexer_1_out27, demultiplexer_1_out28, demultiplexer_1_out29,
       demultiplexer_1_out30, demultiplexer_1_out31;
  wire [2:0] comparator_1_gt;
  wire [4:0] multiplexer_3_out, shift_register_1_q4, shift_register_2_q4, shift_register_3_q4;
  wire [31:0] adder_1_out, and_1_out, demultiplexer_2_out0, demultiplexer_2_out1, demultiplexer_2_out2,
       demultiplexer_2_out3, demultiplexer_2_out4, demultiplexer_2_out5, demultiplexer_2_out6,
       demultiplexer_2_out7, demultiplexer_2_out8, demultiplexer_2_out9, demultiplexer_2_out10,
       demultiplexer_2_out11, demultiplexer_2_out12, demultiplexer_2_out13, demultiplexer_2_out14,
       demultiplexer_2_out15, demultiplexer_2_out16, demultiplexer_2_out17, demultiplexer_2_out18,
       demultiplexer_2_out19, demultiplexer_2_out20, demultiplexer_2_out21, demultiplexer_2_out22,
       demultiplexer_2_out23, demultiplexer_2_out24, demultiplexer_2_out25, demultiplexer_2_out26,
       demultiplexer_2_out27, demultiplexer_2_out28, demultiplexer_2_out29, demultiplexer_2_out30,
       demultiplexer_2_out31, multiplexer_1_out, multiplexer_2_out, multiplexer_4_out, multiplexer_5_out,
       multiplexer_6_out, or_1_out, ram_1_data, register_1_q, register_2_q, register_3_q, register_4_q,
       register_5_q, register_6_q, register_7_q, register_8_q, register_9_q, register_10_q, register_11_q,
       register_12_q, register_13_q, register_14_q, register_15_q, register_16_q, register_17_q,
       register_18_q, register_19_q, register_20_q, register_21_q, register_22_q, register_23_q,
       register_24_q, register_25_q, register_26_q, register_27_q, register_28_q, register_29_q,
       register_30_q, register_31_q, register_32_q, shift_register_4_q31, shift_register_5_q31,
       shift_register_6_q31, shift_register_7_q31, shift_register_8_q7, shift_register_9_q31,
       subtractor_1_out, xor_1_out;

  Register #(.width(32)) register_1 (
    .D(demultiplexer_2_out0), .en(demultiplexer_1_out0), .Q(register_1_q), .clk(clock_1_out));  // open: clr
  Register #(.width(32)) register_2 (
    .D(demultiplexer_2_out4), .en(demultiplexer_1_out4), .Q(register_2_q), .clk(clock_1_out));  // open: clr
  Register #(.width(32)) register_3 (
    .D(demultiplexer_2_out8), .en(demultiplexer_1_out8), .Q(register_3_q), .clk(clock_1_out));  // open: clr
  Register #(.width(32)) register_4 (
    .D(demultiplexer_2_out12), .en(demultiplexer_1_out12), .Q(register_4_q), .clk(clock_1_out));  // open: clr
  Register #(.width(32)) register_5 (
    .D(demultiplexer_2_out16), .en(demultiplexer_1_out16), .Q(register_5_q), .clk(clock_1_out));  // open: clr
  Register #(.width(32)) register_6 (
    .D(demultiplexer_2_out20), .en(demultiplexer_1_out20), .Q(register_6_q), .clk(clock_1_out));  // open: clr
  Register #(.width(32)) register_7 (
    .D(demultiplexer_2_out24), .en(demultiplexer_1_out24), .Q(register_7_q), .clk(clock_1_out));  // open: clr
  Register #(.width(32)) register_8 (
    .D(demultiplexer_2_out28), .en(demultiplexer_1_out28), .Q(register_8_q), .clk(clock_1_out));  // open: clr
  Demultiplexer #(.select(5)) demultiplexer_1 (
    .out0(demultiplexer_1_out0), .out1(demultiplexer_1_out1), .out2(demultiplexer_1_out2),
    .out3(demultiplexer_1_out3), .out4(demultiplexer_1_out4), .out5(demultiplexer_1_out5),
    .out6(demultiplexer_1_out6), .out7(demultiplexer_1_out7), .out8(demultiplexer_1_out8),
    .out9(demultiplexer_1_out9), .out10(demultiplexer_1_out10), .out11(demultiplexer_1_out11),
    .out12(demultiplexer_1_out12), .out13(demultiplexer_1_out13), .out14(demultiplexer_1_out14),
    .out15(demultiplexer_1_out15), .out16(demultiplexer_1_out16), .out17(demultiplexer_1_out17),
    .out18(demultiplexer_1_out18), .out19(demultiplexer_1_out19), .out20(demultiplexer_1_out20),
    .out21(demultiplexer_1_out21), .out22(demultiplexer_1_out22), .out23(demultiplexer_1_out23),
    .out24(demultiplexer_1_out24), .out25(demultiplexer_1_out25), .out26(demultiplexer_1_out26),
    .out27(demultiplexer_1_out27), .out28(demultiplexer_1_out28), .out29(demultiplexer_1_out29),
    .out30(demultiplexer_1_out30), .out31(demultiplexer_1_out31), .in(1'b1), .sel(shift_register_3_q4),
    .en(RF_Demux));
  Register #(.width(32)) register_9 (
    .D(demultiplexer_2_out1), .en(demultiplexer_1_out1), .Q(register_9_q), .clk(clock_1_out));  // open: clr
  Register #(.width(32)) register_10 (
    .D(demultiplexer_2_out5), .en(demultiplexer_1_out5), .Q(register_10_q), .clk(clock_1_out));  // open: clr
  Register #(.width(32)) register_11 (
    .D(demultiplexer_2_out9), .en(demultiplexer_1_out9), .Q(register_11_q), .clk(clock_1_out));  // open: clr
  Register #(.width(32)) register_12 (
    .D(demultiplexer_2_out13), .en(demultiplexer_1_out13), .Q(register_12_q), .clk(clock_1_out));  // open: clr
  Register #(.width(32)) register_13 (
    .D(demultiplexer_2_out17), .en(demultiplexer_1_out17), .Q(register_13_q), .clk(clock_1_out));  // open: clr
  Register #(.width(32)) register_14 (
    .D(demultiplexer_2_out25), .en(demultiplexer_1_out25), .Q(register_14_q), .clk(clock_1_out));  // open: clr
  Register #(.width(32)) register_15 (
    .D(demultiplexer_2_out29), .en(demultiplexer_1_out29), .Q(register_15_q), .clk(clock_1_out));  // open: clr
  Register #(.width(32)) register_16 (
    .D(demultiplexer_2_out21), .en(demultiplexer_1_out21), .Q(register_16_q), .clk(clock_1_out));  // open: clr
  Demultiplexer #(.select(5), .width(32)) demultiplexer_2 (
    .out0(demultiplexer_2_out0), .out1(demultiplexer_2_out1), .out2(demultiplexer_2_out2),
    .out3(demultiplexer_2_out3), .out4(demultiplexer_2_out4), .out5(demultiplexer_2_out5),
    .out6(demultiplexer_2_out6), .out7(demultiplexer_2_out7), .out8(demultiplexer_2_out8),
    .out9(demultiplexer_2_out9), .out10(demultiplexer_2_out10), .out11(demultiplexer_2_out11),
    .out12(demultiplexer_2_out12), .out13(demultiplexer_2_out13), .out14(demultiplexer_2_out14),
    .out15(demultiplexer_2_out15), .out16(demultiplexer_2_out16), .out17(demultiplexer_2_out17),
    .out18(demultiplexer_2_out18), .out19(demultiplexer_2_out19), .out20(demultiplexer_2_out20),
    .out21(demultiplexer_2_out21), .out22(demultiplexer_2_out22), .out23(demultiplexer_2_out23),
    .out24(demultiplexer_2_out24), .out25(demultiplexer_2_out25), .out26(demultiplexer_2_out26),
    .out27(demultiplexer_2_out27), .out28(demultiplexer_2_out28), .out29(demultiplexer_2_out29),
    .out30(demultiplexer_2_out30), .out31(demultiplexer_2_out31), .in(shift_register_9_q31),
    .sel(shift_register_3_q4), .en(RF_Demux));
  Shift_Register #(.length(5)) shift_register_1 (
    .clk(clock_1_out), .load(1'b1), .d0(in_2[25]), .q0(shift_register_1_q4[4]), .d1(in_2[24]),
    .q1(shift_register_1_q4[3]), .d2(in_2[23]), .q2(shift_register_1_q4[2]), .d3(in_2[22]),
    .q3(shift_register_1_q4[1]), .d4(in_2[21]), .q4(shift_register_1_q4[0]));  // open: shift, in, out, clr
  Shift_Register #(.length(5)) shift_register_2 (
    .clk(clock_1_out), .load(1'b1), .d0(shift_register_1_q4[4]), .q0(shift_register_2_q4[4]),
    .d1(shift_register_1_q4[3]), .q1(shift_register_2_q4[3]), .d2(shift_register_1_q4[2]),
    .q2(shift_register_2_q4[2]), .d3(shift_register_1_q4[1]), .q3(shift_register_2_q4[1]),
    .d4(shift_register_1_q4[0]), .q4(shift_register_2_q4[0]));  // open: shift, in, out, clr
  Shift_Register #(.length(5)) shift_register_3 (
    .clk(clock_1_out), .load(1'b1), .d0(shift_register_2_q4[4]), .q0(shift_register_3_q4[4]),
    .d1(shift_register_2_q4[3]), .q1(shift_register_3_q4[3]), .d2(shift_register_2_q4[2]),
    .q2(shift_register_3_q4[2]), .d3(shift_register_2_q4[1]), .q3(shift_register_3_q4[1]),
    .d4(shift_register_2_q4[0]), .q4(shift_register_3_q4[0]));  // open: shift, in, out, clr
  Register #(.width(32)) register_17 (
    .D(demultiplexer_2_out2), .en(demultiplexer_1_out2), .Q(register_17_q), .clk(clock_1_out));  // open: clr
  Register #(.width(32)) register_18 (
    .D(demultiplexer_2_out6), .en(demultiplexer_1_out6), .Q(register_18_q), .clk(clock_1_out));  // open: clr
  Register #(.width(32)) register_19 (
    .D(demultiplexer_2_out10), .en(demultiplexer_1_out10), .Q(register_19_q), .clk(clock_1_out));  // open: clr
  Register #(.width(32)) register_20 (
    .D(demultiplexer_2_out14), .en(demultiplexer_1_out14), .Q(register_20_q), .clk(clock_1_out));  // open: clr
  Register #(.width(32)) register_21 (
    .D(demultiplexer_2_out18), .en(demultiplexer_1_out18), .Q(register_21_q), .clk(clock_1_out));  // open: clr
  Register #(.width(32)) register_22 (
    .D(demultiplexer_2_out22), .en(demultiplexer_1_out22), .Q(register_22_q), .clk(clock_1_out));  // open: clr
  Register #(.width(32)) register_23 (
    .D(demultiplexer_2_out26), .en(demultiplexer_1_out26), .Q(register_23_q), .clk(clock_1_out));  // open: clr
  Register #(.width(32)) register_24 (
    .D(demultiplexer_2_out30), .en(demultiplexer_1_out30), .Q(register_24_q), .clk(clock_1_out));  // open: clr
  Register #(.width(32)) register_25 (
    .D(demultiplexer_2_out3), .en(demultiplexer_1_out3), .Q(register_25_q), .clk(clock_1_out));  // open: clr
  Register #(.width(32)) register_26 (
    .D(demultiplexer_2_out7), .en(demultiplexer_1_out7), .Q(register_26_q), .clk(clock_1_out));  // open: clr
  Register #(.width(32)) register_27 (
    .D(demultiplexer_2_out11), .en(demultiplexer_1_out11), .Q(register_27_q), .clk(clock_1_out));  // open: clr
  Register #(.width(32)) register_28 (
    .D(demultiplexer_2_out15), .en(demultiplexer_1_out15), .Q(register_28_q), .clk(clock_1_out));  // open: clr
  Register #(.width(32)) register_29 (
    .D(demultiplexer_2_out31), .en(demultiplexer_1_out31), .Q(register_29_q), .clk(clock_1_out));  // open: clr
  Register #(.width(32)) register_30 (
    .D(demultiplexer_2_out19), .en(demultiplexer_1_out19), .Q(register_30_q), .clk(clock_1_out));  // open: clr
  Register #(.width(32)) register_31 (
    .D(demultiplexer_2_out23), .en(demultiplexer_1_out23), .Q(register_31_q), .clk(clock_1_out));  // open: clr
  Register #(.width(32)) register_32 (
    .D(demultiplexer_2_out27), .en(demultiplexer_1_out27), .Q(register_32_q), .clk(clock_1_out));  // open: clr
  Multiplexer #(.select(5), .width(32)) multiplexer_1 (
    .in0(register_1_q), .in1(register_9_q), .in2(register_17_q), .in3(register_25_q), .in4(register_2_q),
    .in5(register_10_q), .in6(register_18_q), .in7(register_26_q), .in8(register_3_q), .in9(register_11_q),
    .in10(register_19_q), .in11(register_27_q), .in12(register_4_q), .in13(register_12_q),
    .in14(register_20_q), .in15(register_28_q), .in16(register_5_q), .in17(register_13_q),
    .in18(register_21_q), .in19(register_30_q), .in20(register_6_q), .in21(register_16_q),
    .in22(register_22_q), .in23(register_31_q), .in24(register_7_q), .in25(register_14_q),
    .in26(register_23_q), .in27(register_32_q), .in28(register_8_q), .in29(register_15_q),
    .in30(register_24_q), .in31(register_29_q), .out(multiplexer_1_out), .sel(in_2[20:16]), .en(RF_Mux1));
  Multiplexer #(.select(5), .width(32)) multiplexer_2 (
    .in0(register_1_q), .in1(register_9_q), .in2(register_17_q), .in3(register_25_q), .in4(register_2_q),
    .in5(register_10_q), .in6(register_18_q), .in7(register_26_q), .in8(register_3_q), .in9(register_11_q),
    .in10(register_19_q), .in11(register_27_q), .in12(register_4_q), .in13(register_12_q),
    .in14(register_20_q), .in15(register_28_q), .in16(register_5_q), .in17(register_13_q),
    .in18(register_21_q), .in19(register_30_q), .in20(register_6_q), .in21(register_16_q),
    .in22(register_22_q), .in23(register_31_q), .in24(register_7_q), .in25(register_14_q),
    .in26(register_23_q), .in27(register_32_q), .in28(register_8_q), .in29(register_15_q),
    .in30(register_24_q), .in31(register_29_q), .out(multiplexer_2_out), .sel(multiplexer_3_out), .en(RF_Mux2));
  Multiplexer #(.width(5)) multiplexer_3 (
    .in0(in_2[15:11]), .in1(in_2[25:21]), .out(multiplexer_3_out), .sel(comparator_2_eq), .en(1'b1));
  Shift_Register #(.length(32)) shift_register_4 (
    .clk(clock_1_out), .load(1'b1), .d0(multiplexer_1_out[31]), .q0(shift_register_4_q31[31]),
    .d1(multiplexer_1_out[30]), .q1(shift_register_4_q31[30]), .d2(multiplexer_1_out[29]),
    .q2(shift_register_4_q31[29]), .d3(multiplexer_1_out[28]), .q3(shift_register_4_q31[28]),
    .d4(multiplexer_1_out[27]), .q4(shift_register_4_q31[27]), .d5(multiplexer_1_out[26]),
    .q5(shift_register_4_q31[26]), .d6(multiplexer_1_out[25]), .q6(shift_register_4_q31[25]),
    .d7(multiplexer_1_out[24]), .q7(shift_register_4_q31[24]), .d8(multiplexer_1_out[23]),
    .q8(shift_register_4_q31[23]), .d9(multiplexer_1_out[22]), .q9(shift_register_4_q31[22]),
    .d10(multiplexer_1_out[21]), .q10(shift_register_4_q31[21]), .d11(multiplexer_1_out[20]),
    .q11(shift_register_4_q31[20]), .d12(multiplexer_1_out[19]), .q12(shift_register_4_q31[19]),
    .d13(multiplexer_1_out[18]), .q13(shift_register_4_q31[18]), .d14(multiplexer_1_out[17]),
    .q14(shift_register_4_q31[17]), .d15(multiplexer_1_out[16]), .q15(shift_register_4_q31[16]),
    .d16(multiplexer_1_out[15]), .q16(shift_register_4_q31[15]), .d17(multiplexer_1_out[14]),
    .q17(shift_register_4_q31[14]), .d18(multiplexer_1_out[13]), .q18(shift_register_4_q31[13]),
    .d19(multiplexer_1_out[12]), .q19(shift_register_4_q31[12]), .d20(multiplexer_1_out[11]),
    .q20(shift_register_4_q31[11]), .d21(multiplexer_1_out[10]), .q21(shift_register_4_q31[10]),
    .d22(multiplexer_1_out[9]), .q22(shift_register_4_q31[9]), .d23(multiplexer_1_out[8]),
    .q23(shift_register_4_q31[8]), .d24(multiplexer_1_out[7]), .q24(shift_register_4_q31[7]),
    .d25(multiplexer_1_out[6]), .q25(shift_register_4_q31[6]), .d26(multiplexer_1_out[5]),
    .q26(shift_register_4_q31[5]), .d27(multiplexer_1_out[4]), .q27(shift_register_4_q31[4]),
    .d28(multiplexer_1_out[3]), .q28(shift_register_4_q31[3]), .d29(multiplexer_1_out[2]),
    .q29(shift_register_4_q31[2]), .d30(multiplexer_1_out[1]), .q30(shift_register_4_q31[1]),
    .d31(multiplexer_1_out[0]), .q31(shift_register_4_q31[0]));  // open: shift, in, out, clr
  Shift_Register #(.length(32)) shift_register_5 (
    .clk(clock_1_out), .load(1'b1), .d0(1'b0), .q0(shift_register_5_q31[31]), .d1(1'b0),
    .q1(shift_register_5_q31[30]), .d2(1'b0), .q2(shift_register_5_q31[29]), .d3(1'b0),
    .q3(shift_register_5_q31[28]), .d4(1'b0), .q4(shift_register_5_q31[27]), .d5(1'b0),
    .q5(shift_register_5_q31[26]), .d6(1'b0), .q6(shift_register_5_q31[25]), .d7(1'b0),
    .q7(shift_register_5_q31[24]), .d8(1'b0), .q8(shift_register_5_q31[23]), .d9(1'b0),
    .q9(shift_register_5_q31[22]), .d10(1'b0), .q10(shift_register_5_q31[21]), .d11(1'b0),
    .q11(shift_register_5_q31[20]), .d12(1'b0), .q12(shift_register_5_q31[19]), .d13(1'b0),
    .q13(shift_register_5_q31[18]), .d14(1'b0), .q14(shift_register_5_q31[17]), .d15(1'b0),
    .q15(shift_register_5_q31[16]), .d16(in_2[15]), .q16(shift_register_5_q31[15]), .d17(in_2[14]),
    .q17(shift_register_5_q31[14]), .d18(in_2[13]), .q18(shift_register_5_q31[13]), .d19(in_2[12]),
    .q19(shift_register_5_q31[12]), .d20(in_2[11]), .q20(shift_register_5_q31[11]), .d21(in_2[10]),
    .q21(shift_register_5_q31[10]), .d22(in_2[9]), .q22(shift_register_5_q31[9]), .d23(in_2[8]),
    .q23(shift_register_5_q31[8]), .d24(in_2[7]), .q24(shift_register_5_q31[7]), .d25(in_2[6]),
    .q25(shift_register_5_q31[6]), .d26(in_2[5]), .q26(shift_register_5_q31[5]), .d27(in_2[4]),
    .q27(shift_register_5_q31[4]), .d28(in_2[3]), .q28(shift_register_5_q31[3]), .d29(in_2[2]),
    .q29(shift_register_5_q31[2]), .d30(in_2[1]), .q30(shift_register_5_q31[1]), .d31(in_2[0]),
    .q31(shift_register_5_q31[0]));  // open: shift, in, out, clr
  Adder #(.width(32)) adder_1 (
    .a(shift_register_4_q31), .b(multiplexer_4_out), .out(adder_1_out), .cin(1'b0), .cout(Addition_cary));
  Subtractor #(.width(32)) subtractor_1 (
    .a(shift_register_4_q31), .b(multiplexer_4_out), .out(subtractor_1_out), .bin(1'b0), .bout(out_10));
  assign or_1_out = shift_register_4_q31 | multiplexer_4_out;  // OR_Gate or_1, 32 bits wide
  assign and_1_out = shift_register_4_q31 & multiplexer_4_out;  // AND_Gate and_1, 32 bits wide
  assign xor_1_out = shift_register_4_q31 ^ multiplexer_4_out;  // XOR_Gate xor_1, 32 bits wide
  Comparator #(.width(32), .mode("unsigned")) comparator_1 (
    .a(shift_register_4_q31), .b(multiplexer_4_out), .gt(comparator_1_gt[0]), .eq(comparator_1_gt[1]),
    .lt(comparator_1_gt[2]));
  Multiplexer #(.width(32)) multiplexer_4 (
    .in0(shift_register_5_q31), .in1(shift_register_6_q31), .out(multiplexer_4_out), .sel(in_2[27]), .en(MUXB));
  Shift_Register #(.length(32)) shift_register_6 (
    .in(clock_1_out), .clk(clock_1_out), .load(1'b1), .d0(multiplexer_2_out[31]),
    .q0(shift_register_6_q31[31]), .d1(multiplexer_2_out[30]), .q1(shift_register_6_q31[30]),
    .d2(multiplexer_2_out[29]), .q2(shift_register_6_q31[29]), .d3(multiplexer_2_out[28]),
    .q3(shift_register_6_q31[28]), .d4(multiplexer_2_out[27]), .q4(shift_register_6_q31[27]),
    .d5(multiplexer_2_out[26]), .q5(shift_register_6_q31[26]), .d6(multiplexer_2_out[25]),
    .q6(shift_register_6_q31[25]), .d7(multiplexer_2_out[24]), .q7(shift_register_6_q31[24]),
    .d8(multiplexer_2_out[23]), .q8(shift_register_6_q31[23]), .d9(multiplexer_2_out[22]),
    .q9(shift_register_6_q31[22]), .d10(multiplexer_2_out[21]), .q10(shift_register_6_q31[21]),
    .d11(multiplexer_2_out[20]), .q11(shift_register_6_q31[20]), .d12(multiplexer_2_out[19]),
    .q12(shift_register_6_q31[19]), .d13(multiplexer_2_out[18]), .q13(shift_register_6_q31[18]),
    .d14(multiplexer_2_out[17]), .q14(shift_register_6_q31[17]), .d15(multiplexer_2_out[16]),
    .q15(shift_register_6_q31[16]), .d16(multiplexer_2_out[15]), .q16(shift_register_6_q31[15]),
    .d17(multiplexer_2_out[14]), .q17(shift_register_6_q31[14]), .d18(multiplexer_2_out[13]),
    .q18(shift_register_6_q31[13]), .d19(multiplexer_2_out[12]), .q19(shift_register_6_q31[12]),
    .d20(multiplexer_2_out[11]), .q20(shift_register_6_q31[11]), .d21(multiplexer_2_out[10]),
    .q21(shift_register_6_q31[10]), .d22(multiplexer_2_out[9]), .q22(shift_register_6_q31[9]),
    .d23(multiplexer_2_out[8]), .q23(shift_register_6_q31[8]), .d24(multiplexer_2_out[7]),
    .q24(shift_register_6_q31[7]), .d25(multiplexer_2_out[6]), .q25(shift_register_6_q31[6]),
    .d26(multiplexer_2_out[5]), .q26(shift_register_6_q31[5]), .d27(multiplexer_2_out[4]),
    .q27(shift_register_6_q31[4]), .d28(multiplexer_2_out[3]), .q28(shift_register_6_q31[3]),
    .d29(multiplexer_2_out[2]), .q29(shift_register_6_q31[2]), .d30(multiplexer_2_out[1]),
    .q30(shift_register_6_q31[1]), .d31(multiplexer_2_out[0]), .q31(shift_register_6_q31[0]));  // open: shift, out, clr
  Shift_Register #(.length(32)) shift_register_7 (
    .clk(clock_1_out), .load(1'b1), .d0(shift_register_6_q31[31]), .q0(shift_register_7_q31[31]),
    .d1(shift_register_6_q31[30]), .q1(shift_register_7_q31[30]), .d2(shift_register_6_q31[29]),
    .q2(shift_register_7_q31[29]), .d3(shift_register_6_q31[28]), .q3(shift_register_7_q31[28]),
    .d4(shift_register_6_q31[27]), .q4(shift_register_7_q31[27]), .d5(shift_register_6_q31[26]),
    .q5(shift_register_7_q31[26]), .d6(shift_register_6_q31[25]), .q6(shift_register_7_q31[25]),
    .d7(shift_register_6_q31[24]), .q7(shift_register_7_q31[24]), .d8(shift_register_6_q31[23]),
    .q8(shift_register_7_q31[23]), .d9(shift_register_6_q31[22]), .q9(shift_register_7_q31[22]),
    .d10(shift_register_6_q31[21]), .q10(shift_register_7_q31[21]), .d11(shift_register_6_q31[20]),
    .q11(shift_register_7_q31[20]), .d12(shift_register_6_q31[19]), .q12(shift_register_7_q31[19]),
    .d13(shift_register_6_q31[18]), .q13(shift_register_7_q31[18]), .d14(shift_register_6_q31[17]),
    .q14(shift_register_7_q31[17]), .d15(shift_register_6_q31[16]), .q15(shift_register_7_q31[16]),
    .d16(shift_register_6_q31[15]), .q16(shift_register_7_q31[15]), .d17(shift_register_6_q31[14]),
    .q17(shift_register_7_q31[14]), .d18(shift_register_6_q31[13]), .q18(shift_register_7_q31[13]),
    .d19(shift_register_6_q31[12]), .q19(shift_register_7_q31[12]), .d20(shift_register_6_q31[11]),
    .q20(shift_register_7_q31[11]), .d21(shift_register_6_q31[10]), .q21(shift_register_7_q31[10]),
    .d22(shift_register_6_q31[9]), .q22(shift_register_7_q31[9]), .d23(shift_register_6_q31[8]),
    .q23(shift_register_7_q31[8]), .d24(shift_register_6_q31[7]), .q24(shift_register_7_q31[7]),
    .d25(shift_register_6_q31[6]), .q25(shift_register_7_q31[6]), .d26(shift_register_6_q31[5]),
    .q26(shift_register_7_q31[5]), .d27(shift_register_6_q31[4]), .q27(shift_register_7_q31[4]),
    .d28(shift_register_6_q31[3]), .q28(shift_register_7_q31[3]), .d29(shift_register_6_q31[2]),
    .q29(shift_register_7_q31[2]), .d30(shift_register_6_q31[1]), .q30(shift_register_7_q31[1]),
    .d31(shift_register_6_q31[0]), .q31(shift_register_7_q31[0]));  // open: shift, in, out, clr
  Shift_Register #(.length(32)) shift_register_8 (
    .clk(clock_1_out), .load(1'b1), .d0(multiplexer_5_out[31]), .q0(shift_register_8_q7[31]),
    .d1(multiplexer_5_out[30]), .q1(shift_register_8_q7[30]), .d2(multiplexer_5_out[29]),
    .q2(shift_register_8_q7[29]), .d3(multiplexer_5_out[28]), .q3(shift_register_8_q7[28]),
    .d4(multiplexer_5_out[27]), .q4(shift_register_8_q7[27]), .d5(multiplexer_5_out[26]),
    .q5(shift_register_8_q7[26]), .d6(multiplexer_5_out[25]), .q6(shift_register_8_q7[25]),
    .d7(multiplexer_5_out[24]), .q7(shift_register_8_q7[24]), .d8(multiplexer_5_out[23]),
    .q8(shift_register_8_q7[23]), .d9(multiplexer_5_out[22]), .q9(shift_register_8_q7[22]),
    .d10(multiplexer_5_out[21]), .q10(shift_register_8_q7[21]), .d11(multiplexer_5_out[20]),
    .q11(shift_register_8_q7[20]), .d12(multiplexer_5_out[19]), .q12(shift_register_8_q7[19]),
    .d13(multiplexer_5_out[18]), .q13(shift_register_8_q7[18]), .d14(multiplexer_5_out[17]),
    .q14(shift_register_8_q7[17]), .d15(multiplexer_5_out[16]), .q15(shift_register_8_q7[16]),
    .d16(multiplexer_5_out[15]), .q16(shift_register_8_q7[15]), .d17(multiplexer_5_out[14]),
    .q17(shift_register_8_q7[14]), .d18(multiplexer_5_out[13]), .q18(shift_register_8_q7[13]),
    .d19(multiplexer_5_out[12]), .q19(shift_register_8_q7[12]), .d20(multiplexer_5_out[11]),
    .q20(shift_register_8_q7[11]), .d21(multiplexer_5_out[10]), .q21(shift_register_8_q7[10]),
    .d22(multiplexer_5_out[9]), .q22(shift_register_8_q7[9]), .d23(multiplexer_5_out[8]),
    .q23(shift_register_8_q7[8]), .d24(multiplexer_5_out[7]), .q24(shift_register_8_q7[7]),
    .d25(multiplexer_5_out[6]), .q25(shift_register_8_q7[6]), .d26(multiplexer_5_out[5]),
    .q26(shift_register_8_q7[5]), .d27(multiplexer_5_out[4]), .q27(shift_register_8_q7[4]),
    .d28(multiplexer_5_out[3]), .q28(shift_register_8_q7[3]), .d29(multiplexer_5_out[2]),
    .q29(shift_register_8_q7[2]), .d30(multiplexer_5_out[1]), .q30(shift_register_8_q7[1]),
    .d31(multiplexer_5_out[0]), .q31(shift_register_8_q7[0]));  // open: shift, in, out, clr
  Shift_Register #(.length(32)) shift_register_9 (
    .clk(clock_1_out), .load(1'b1), .d0(multiplexer_6_out[31]), .q0(shift_register_9_q31[31]),
    .d1(multiplexer_6_out[30]), .q1(shift_register_9_q31[30]), .d2(multiplexer_6_out[29]),
    .q2(shift_register_9_q31[29]), .d3(multiplexer_6_out[28]), .q3(shift_register_9_q31[28]),
    .d4(multiplexer_6_out[27]), .q4(shift_register_9_q31[27]), .d5(multiplexer_6_out[26]),
    .q5(shift_register_9_q31[26]), .d6(multiplexer_6_out[25]), .q6(shift_register_9_q31[25]),
    .d7(multiplexer_6_out[24]), .q7(shift_register_9_q31[24]), .d8(multiplexer_6_out[23]),
    .q8(shift_register_9_q31[23]), .d9(multiplexer_6_out[22]), .q9(shift_register_9_q31[22]),
    .d10(multiplexer_6_out[21]), .q10(shift_register_9_q31[21]), .d11(multiplexer_6_out[20]),
    .q11(shift_register_9_q31[20]), .d12(multiplexer_6_out[19]), .q12(shift_register_9_q31[19]),
    .d13(multiplexer_6_out[18]), .q13(shift_register_9_q31[18]), .d14(multiplexer_6_out[17]),
    .q14(shift_register_9_q31[17]), .d15(multiplexer_6_out[16]), .q15(shift_register_9_q31[16]),
    .d16(multiplexer_6_out[15]), .q16(shift_register_9_q31[15]), .d17(multiplexer_6_out[14]),
    .q17(shift_register_9_q31[14]), .d18(multiplexer_6_out[13]), .q18(shift_register_9_q31[13]),
    .d19(multiplexer_6_out[12]), .q19(shift_register_9_q31[12]), .d20(multiplexer_6_out[11]),
    .q20(shift_register_9_q31[11]), .d21(multiplexer_6_out[10]), .q21(shift_register_9_q31[10]),
    .d22(multiplexer_6_out[9]), .q22(shift_register_9_q31[9]), .d23(multiplexer_6_out[8]),
    .q23(shift_register_9_q31[8]), .d24(multiplexer_6_out[7]), .q24(shift_register_9_q31[7]),
    .d25(multiplexer_6_out[6]), .q25(shift_register_9_q31[6]), .d26(multiplexer_6_out[5]),
    .q26(shift_register_9_q31[5]), .d27(multiplexer_6_out[4]), .q27(shift_register_9_q31[4]),
    .d28(multiplexer_6_out[3]), .q28(shift_register_9_q31[3]), .d29(multiplexer_6_out[2]),
    .q29(shift_register_9_q31[2]), .d30(multiplexer_6_out[1]), .q30(shift_register_9_q31[1]),
    .d31(multiplexer_6_out[0]), .q31(shift_register_9_q31[0]));  // open: shift, in, out, clr
  Multiplexer #(.select(4), .width(32)) multiplexer_5 (
    .in0(adder_1_out), .in1(subtractor_1_out), .in2(or_1_out), .in3(and_1_out), .in4(xor_1_out),
    .in5({{29{1'b0}}, comparator_1_gt}), .in13(adder_1_out), .in14(adder_1_out), .in15(adder_1_out),
    .out(multiplexer_5_out), .sel(in_2[31:28]), .en(ALU_Mux));  // open: in6, in7, in8, in9, in10, in11, in12
  Multiplexer #(.width(32)) multiplexer_6 (
    .in0(shift_register_8_q7), .in1(ram_1_data), .out(multiplexer_6_out), .sel(in_2[26]), .en(MUXY));
  Clock clock_1 (.out(clock_1_out));
  Comparator #(.width(4), .mode("unsigned")) comparator_2 (
    .a(in_2[31:28]), .b(4'b1101), .eq(comparator_2_eq));  // open: gt, lt
  Comparator #(.width(4), .mode("unsigned")) comparator_3 (
    .a(in_2[31:28]), .b(4'b1111), .eq(comparator_3_eq));  // open: gt, lt
  RAM #(.addrWidth(24), .dataWidth(32), .bus("separate")) ram_1 (
    .addr(shift_register_8_q7[23:0]), .din(shift_register_7_q31), .data(ram_1_data), .str(comparator_2_eq),
    .sel(1'b1), .clk(clock_1_out), .ld(comparator_3_eq), .clr(Clear_memory));

  // Notes on the sheet:
  //   Ra
  //   immediate
  //   Rb
  //   Enable pins
  //   Rm
  //   Rz
  //   Clock
  //   ADDRESS
  //   Ry
  //   opcode
  //   demux
  //   mux for a
  //   Mux for b
  //   DATA FROM MEMORY
  //   immediate
  //   subtraction carry
endmodule
